# Fritzing sketch Circuit Diagram (saved by Fritzing 0.9.2b)
breadboards: 1

parts:
  R1 = Resistor [tolerance=±5% resistance=330 package=THT]
  R2 = Resistor [tolerance=±5% resistance=160 package=THT]
  R3 = Resistor [tolerance=±20% resistance=22k package=THT]
  R4 = Resistor [tolerance=±5% resistance=50 package=THT]
  J1 = Piezo Speaker  # not connected
  Part2 = Arduino Ethernet Shield (Rev3)
  S1 = Pushbutton [package=THT]
  LED1 = RGB LED (com. cathode, rgb) [package="5 mm [THT]"]

nets:
  N1: R1.Pin_0, Part2.A0
  N2: R1.Pin_1, LED1.red_anode
  N3: R2.Pin_0, Part2.A1
  N4: R2.Pin_1, LED1.green_anode
  N5: R3.Pin_0, Part2.A2
  N6: R3.Pin_1, LED1.blue_anode
  N7: R4.Pin_0, Part2.PWM_D5
  N8: Part2.A3, S1.leg0
  N9: Part2.5V, LED1.common_cathode
  N10: Part2.GND, S1.leg1

notes:
  Morse Key
